# Fritzing sketch Weather (saved by Fritzing 0.9.2b)
breadboards: 1

parts:
  Part1 = Arduino Uno (Rev3)  # not connected
  Part2 = Arduino Mega 2560 (Rev3)
  R1 = Resistor [tolerance=±5% resistance=330 package=THT]
  LED1 = LED - 5mm [color="Red (633nm)" package="5 mm [THT]"]
  Part_1 = Weather Shield [part_number=DEV-12081]  # not connected
  Part3 = Arduino GPS Shield
  Part_2 = Weather Shield [part_number=DEV-12081]

nets:
  N1: Part2.D19/RX1, Part_2.TX
  N2: Part2.D18/TX1, Part_2.RX
  GND: Part2.GND, R1.Pin_0, Part3.GND, Part_2.GND
  N3: Part2.D13_PWM, LED1.anode
  5V: Part2.5V, Part3.5VIN, Part_2.5V
  N4: Part2.D2_PWM, Part3.D_RX
  N5: Part2.D7_PWM, Part3.D7
  N6: Part2.D22, Part3.D10
  N7: Part2.D50, Part3.D12
  N8: Part2.D51, Part3.D11
  N9: Part2.D52, Part3.D13
  N10: R1.Pin_1, LED1.cathode

notes:
  The Mega parses the weather data the Uno sends, and relays it over the net
  The Uno uses the weather shiels and send the weather date to the Mega via the serial.
  The Mega gets the power and transmits it to the Uno.
  The weather shield rides on top of the uno.
  I used the GPS shield in lieu of the WiFi Shield as they have similar layout.
  USED THE SAME NUMBERS!

custom parts:
  Weather Shield: Weather Shield includes: - ALS-PT19 Light Sensor - HTU21D Humidity Sensor - MPL3115A2 - TEMT6000 Check out the product page on www.sparkfun.com for documentation!
